// Logisim project 11_19_19 Design 2.circ as structural Verilog: 1 circuit, main circuit main
module main (
  input  in_1,
  input  BREAK,
  input  LEFT,
  input  RIGHT
);

  wire clock_1_out, clock_2_out, clock_3_out, d_ff_1_q, d_ff_2_q, d_ff_3_q, d_ff_4_q, d_ff_5_q, d_ff_5_qn,
       d_ff_6_q, d_ff_6_qn, multiplexer_1_out, multiplexer_2_out, multiplexer_3_out, multiplexer_4_out,
       multiplexer_5_out, multiplexer_6_out, multiplexer_7_out, multiplexer_8_out, multiplexer_9_out,
       multiplexer_10_out;

  Clock clock_1 (.out(clock_1_out));
  Clock clock_2 (.out(clock_2_out));
  Multiplexer #(.select(2)) multiplexer_1 (
    .in0(BREAK), .in1(d_ff_6_q), .in2(BREAK), .in3(multiplexer_3_out), .out(multiplexer_1_out),
    .sel({RIGHT, LEFT}), .en(1'b1));
  LED led_1 (.in(multiplexer_1_out));
  D_Flip_Flop d_ff_1 (.clk(clock_1_out), .D(d_ff_5_qn), .Q(d_ff_1_q));  // open: Qn, preset, en, reset
  LED led_2 (.in(d_ff_5_q));
  LED led_3 (.in(d_ff_3_q));
  D_Flip_Flop d_ff_2 (
    .clk(clock_2_out), .D(d_ff_6_qn), .Q(d_ff_2_q), .reset(multiplexer_5_out));  // open: Qn, preset, en
  Multiplexer #(.select(2)) multiplexer_2 (
    .in0(BREAK), .in1(d_ff_4_q), .in2(BREAK), .in3(multiplexer_3_out), .out(multiplexer_2_out),
    .sel({RIGHT, LEFT}), .en(1'b1));
  LED led_4 (.in(multiplexer_2_out));
  D_Flip_Flop d_ff_3 (.clk(clock_1_out), .D(d_ff_1_q), .Q(d_ff_3_q));  // open: Qn, preset, en, reset
  LED led_5 (.in(d_ff_1_q));
  LED led_6 (.in(d_ff_1_q));
  D_Flip_Flop d_ff_4 (
    .clk(clock_2_out), .D(d_ff_2_q), .Q(d_ff_4_q), .reset(multiplexer_5_out));  // open: Qn, preset, en
  Multiplexer multiplexer_3 (.in0(clock_2_out), .in1(BREAK), .out(multiplexer_3_out), .sel(BREAK), .en(1'b1));
  Multiplexer #(.select(2)) multiplexer_4 (
    .in0(BREAK), .in1(d_ff_2_q), .in2(BREAK), .in3(multiplexer_3_out), .out(multiplexer_4_out),
    .sel({RIGHT, LEFT}), .en(1'b1));
  LED led_7 (.in(multiplexer_4_out));
  D_Flip_Flop d_ff_5 (.clk(clock_1_out), .D(d_ff_3_q), .Q(d_ff_5_q), .Qn(d_ff_5_qn));  // open: preset, en, reset
  LED led_8 (.in(d_ff_3_q));
  LED led_9 (.in(d_ff_5_q));
  D_Flip_Flop d_ff_6 (
    .clk(clock_2_out), .D(d_ff_4_q), .Q(d_ff_6_q), .Qn(d_ff_6_qn), .reset(multiplexer_5_out));  // open: preset, en
  Clock clock_3 (.out(clock_3_out));
  Multiplexer multiplexer_5 (
    .in0(multiplexer_7_out), .in1(multiplexer_8_out), .out(multiplexer_5_out), .sel(RIGHT), .en(1'b1));
  Multiplexer #(.select(2)) multiplexer_6 (
    .in0(BREAK), .in1(BREAK), .in2(d_ff_2_q), .in3(multiplexer_3_out), .out(multiplexer_6_out),
    .sel({RIGHT, LEFT}), .en(1'b1));
  LED led_10 (.in(multiplexer_6_out));
  LED led_11 (.in(clock_3_out));
  LED led_12 (.in(clock_3_out));
  Multiplexer multiplexer_7 (.in0(1'b1), .in1(1'b0), .out(multiplexer_7_out), .sel(LEFT), .en(1'b1));
  Multiplexer multiplexer_8 (.in0(1'b0), .in1(1'b1), .out(multiplexer_8_out), .sel(LEFT), .en(1'b1));
  Multiplexer #(.select(2)) multiplexer_9 (
    .in0(BREAK), .in1(BREAK), .in2(d_ff_4_q), .in3(multiplexer_3_out), .out(multiplexer_9_out),
    .sel({RIGHT, LEFT}), .en(1'b1));
  LED led_13 (.in(multiplexer_9_out));
  LED led_14 (.in(clock_3_out));
  LED led_15 (.in(clock_3_out));
  Multiplexer #(.select(2)) multiplexer_10 (
    .in0(BREAK), .in1(BREAK), .in2(d_ff_6_q), .in3(multiplexer_3_out), .out(multiplexer_10_out),
    .sel({RIGHT, LEFT}), .en(1'b1));
  LED led_16 (.in(multiplexer_10_out));
  LED led_17 (.in(clock_3_out));
  LED led_18 (.in(clock_3_out));
  LED led_19 (.in(in_1));
  LED led_20 (.in(in_1));
  LED led_21 (.in(in_1));
  LED led_22 (.in(in_1));
  LED led_23 (.in(in_1));
  LED led_24 (.in(in_1));
endmodule
