// Logisim project 11_19_19 Design 5.circ as structural Verilog: 1 circuit, main circuit main
module main (
  input  in_1,
  input  RIGHT,
  input  LEFT,
  input  BREAK,
  output out_5,
  output out_6,
  output out_7
);

  wire clock_1_out, d_ff_1_q, d_ff_2_q, d_ff_3_q, d_ff_3_qn, n7400_1_p2, n7474_1_p3, n7474_2_p9, n74153_1_p3,
       n74153_1_p7, n74153_1_p12, n74153_1_p16, n74157_1_p4, n74157_1_p7, n74157_1_p13, n74157_2_p4,
       n74157_2_p10, n74157_2_p13, not_1_out, not_2_out;

  // _74153 74153_1: pin names not known; wires that end beside it: 1'b0, LEFT, n74153_1_p3, 1'b1, 1'b1, 1'b1, n74153_1_p7, 1'b0, 1'b1, 1'b0, RIGHT, n74153_1_p12, 1'b1, 1'b1, 1'b0, n74153_1_p16
  Clock clock_1 (.out(clock_1_out));
  Clock clock_2 (.out(n74153_1_p3));
  not not_1 (not_1_out, n74153_1_p16);
  not not_2 (not_2_out, n74153_1_p7);
  // _7400 7400_1: pin names not known; wires that end beside it: n74153_1_p3, n7400_1_p2, n74153_1_p12, BREAK, BREAK, n7400_1_p2, 1'b0, 1'b1
  LED led_1 (.in(n74157_1_p4));
  D_Flip_Flop d_ff_1 (.clk(clock_1_out), .D(d_ff_3_qn), .Q(d_ff_1_q));  // open: Qn, preset, en, reset
  LED led_2 (.in(d_ff_2_q));
  LED led_3 (.in(d_ff_3_q));
  LED led_4 (.in(n74157_1_p7));
  D_Flip_Flop d_ff_2 (.clk(clock_1_out), .D(d_ff_1_q), .Q(d_ff_2_q));  // open: Qn, preset, en, reset
  LED led_5 (.in(d_ff_1_q));
  LED led_6 (.in(d_ff_1_q));
  // _7474 7474_1: pin names not known; wires that end beside it: clock_1_out, not_1_out, n7474_1_p3, n74153_1_p3, not_2_out, out_5, 1'b0, 1'b1, not_1_out, out_5, n74153_1_p3, not_2_out, out_6
  // _74157 74157_1: pin names not known; wires that end beside it: LEFT, BREAK, out_7, n74157_1_p4, BREAK, out_6, n74157_1_p7, 1'b0, 1'b1, 1'b0, BREAK, out_5, n74157_1_p13
  LED led_7 (.in(n74157_1_p13));
  D_Flip_Flop d_ff_3 (.clk(clock_1_out), .D(d_ff_2_q), .Q(d_ff_3_q), .Qn(d_ff_3_qn));  // open: preset, en, reset
  LED led_8 (.in(d_ff_3_q));
  LED led_9 (.in(d_ff_2_q));
  // _7474 7474_2: pin names not known; wires that end beside it: not_1_out, out_6, n74153_1_p3, not_2_out, out_7, n7474_1_p3, 1'b0, 1'b1, n7474_2_p9
  // _74157 74157_2: pin names not known; wires that end beside it: RIGHT, BREAK, out_5, n74157_2_p4, 1'b0, 1'b1, 1'b0, BREAK, out_7, n74157_2_p10, BREAK, out_6, n74157_2_p13, n74157_2_p13
  LED led_10 (.in(n74157_2_p4));
  Clock clock_3 (.out(n7474_2_p9));
  LED led_11 (.in(n74157_2_p13));
  LED led_12 (.in(n7474_2_p9));
  LED led_13 (.in(n7474_2_p9));
  LED led_14 (.in(n74157_2_p10));
  LED led_15 (.in(n7474_2_p9));
  LED led_16 (.in(n7474_2_p9));
  LED led_17 (.in(n7474_2_p9));
  LED led_18 (.in(n7474_2_p9));
  LED led_19 (.in(in_1));
  LED led_20 (.in(in_1));
  LED led_21 (.in(in_1));
  LED led_22 (.in(in_1));
  LED led_23 (.in(in_1));
  LED led_24 (.in(in_1));

  // Notes on the sheet:
  //   PRESET
  //   CLEAR
endmodule
