// Logisim project 12_1_19 Design 4.circ as structural Verilog: 1 circuit, main circuit main
module main (
  input  in_1,
  input  BREAK,
  input  LEFT,
  input  RIGHT
);

  wire clock_1_out, clock_2_out, clock_3_out, d_ff_1_q, d_ff_2_q, d_ff_3_q, d_ff_4_q, d_ff_5_q, d_ff_5_qn,
       d_ff_6_q, d_ff_6_qn, multiplexer_1_out, multiplexer_2_out, multiplexer_3_out, multiplexer_4_out,
       multiplexer_5_out, multiplexer_6_out, or_1_out, undriven, xnor_1_out;

  LED led_1 (.in(multiplexer_1_out));
  Clock clock_1 (.out(clock_1_out));
  Clock clock_2 (.out(clock_2_out));
  xnor xnor_1 (xnor_1_out, RIGHT, LEFT);
  or or_1 (or_1_out, BREAK, clock_2_out);
  Multiplexer #(.select(2)) multiplexer_1 (
    .in0(BREAK), .in1(d_ff_6_q), .in2(BREAK), .in3(or_1_out), .out(multiplexer_1_out), .sel({RIGHT, LEFT}));  // open: en
  LED led_2 (.in(multiplexer_2_out));
  D_Flip_Flop d_ff_1 (.clk(clock_1_out), .D(d_ff_5_qn), .Q(d_ff_1_q));  // open: Qn, preset, en, reset
  LED led_3 (.in(d_ff_5_q));
  LED led_4 (.in(d_ff_3_q));
  D_Flip_Flop d_ff_2 (
    .clk(clock_2_out), .D(d_ff_6_qn), .Q(d_ff_2_q), .preset(undriven), .reset(xnor_1_out));  // open: Qn, en
  Multiplexer #(.select(2)) multiplexer_2 (
    .in0(BREAK), .in1(d_ff_4_q), .in2(BREAK), .in3(or_1_out), .out(multiplexer_2_out), .sel({RIGHT, LEFT}));  // open: en
  LED led_5 (.in(multiplexer_3_out));
  D_Flip_Flop d_ff_3 (.clk(clock_1_out), .D(d_ff_1_q), .Q(d_ff_3_q));  // open: Qn, preset, en, reset
  LED led_6 (.in(d_ff_1_q));
  LED led_7 (.in(d_ff_1_q));
  D_Flip_Flop d_ff_4 (
    .clk(clock_2_out), .D(d_ff_2_q), .Q(d_ff_4_q), .preset(undriven), .reset(xnor_1_out));  // open: Qn, en
  Multiplexer #(.select(2)) multiplexer_3 (
    .in0(BREAK), .in1(d_ff_2_q), .in2(BREAK), .in3(or_1_out), .out(multiplexer_3_out), .sel({RIGHT, LEFT}));  // open: en
  D_Flip_Flop d_ff_5 (.clk(clock_1_out), .D(d_ff_3_q), .Q(d_ff_5_q), .Qn(d_ff_5_qn));  // open: preset, en, reset
  LED led_8 (.in(d_ff_3_q));
  LED led_9 (.in(d_ff_5_q));
  D_Flip_Flop d_ff_6 (
    .clk(clock_2_out), .D(d_ff_4_q), .Q(d_ff_6_q), .Qn(d_ff_6_qn), .preset(undriven), .reset(xnor_1_out));  // open: en
  Multiplexer #(.select(2)) multiplexer_4 (
    .in0(BREAK), .in1(BREAK), .in2(d_ff_2_q), .in3(or_1_out), .out(multiplexer_4_out), .sel({RIGHT, LEFT}));  // open: en
  Clock clock_3 (.out(clock_3_out));
  Multiplexer #(.select(2)) multiplexer_5 (
    .in0(BREAK), .in1(BREAK), .in2(d_ff_4_q), .in3(or_1_out), .out(multiplexer_5_out), .sel({RIGHT, LEFT}));  // open: en
  LED led_10 (.in(multiplexer_4_out));
  LED led_11 (.in(clock_3_out));
  LED led_12 (.in(clock_3_out));
  Multiplexer #(.select(2)) multiplexer_6 (
    .in0(BREAK), .in1(BREAK), .in2(d_ff_6_q), .in3(or_1_out), .out(multiplexer_6_out), .sel({RIGHT, LEFT}));  // open: en
  LED led_13 (.in(multiplexer_5_out));
  LED led_14 (.in(clock_3_out));
  LED led_15 (.in(clock_3_out));
  LED led_16 (.in(multiplexer_6_out));
  LED led_17 (.in(clock_3_out));
  LED led_18 (.in(clock_3_out));
  LED led_19 (.in(in_1));
  LED led_20 (.in(in_1));
  LED led_21 (.in(in_1));
  LED led_22 (.in(in_1));
  LED led_23 (.in(in_1));
  LED led_24 (.in(in_1));
endmodule
